// Logisim project 1.3_NAND_1.circ as structural Verilog: 1 circuit, main circuit main
module main (
  input  in_1,
  input  in_2,
  input  in_3,
  input  in_4,
  input  in_5,
  input  in_6,
  input  in_7
);

  wire and_1_out, nand_1_out, nand_2_out, nand_3_out, nand_4_out, nand_5_out, nand_6_out, nand_7_out,
       nand_8_out, nand_9_out, nand_10_out, nor_1_out;

  and and_1 (and_1_out, in_1, in_3);
  nand nand_1 (nand_1_out, in_7, in_7);
  // Probe on and_1_out
  nand nand_2 (nand_2_out, in_3, in_1);
  nor nor_1 (nor_1_out, in_5, in_6);
  not nand_3 (nand_3_out, in_6);  // NAND_Gate
  not nand_4 (nand_4_out, in_5);  // NAND_Gate
  // Probe on nand_1_out
  // Probe on nand_5_out
  not nand_5 (nand_5_out, nand_2_out);  // NAND_Gate
  // Probe on nor_1_out
  nand nand_6 (nand_6_out, nand_3_out, nand_4_out);
  not nand_7 (nand_7_out, nand_6_out);  // NAND_Gate
  // Probe on nand_7_out
  nand nand_8 (nand_8_out, in_2, in_2);
  nand nand_9 (nand_9_out, in_4, in_4);
  nand nand_10 (nand_10_out, nand_8_out, nand_9_out);
  // Probe on nand_10_out

  // Notes on the sheet:
  //   1.3 - Create a NOT, 2 input NOR and 2 input AND using only 2 input NAND's
endmodule
