// Logisim project 1.9_karnaugh_implementation.circ as structural Verilog: 1 circuit, main circuit main
module main (
  input  A,
  input  B,
  input  C,
  input  D,
  input  E
);

  wire and_1_out, and_2_out, and_3_out, and_4_out, and_5_out, not_1_out, not_2_out, not_3_out, not_4_out,
       or_1_out, or_2_out;

  not not_1 (not_1_out, A);
  not not_2 (not_2_out, C);
  not not_3 (not_3_out, D);
  not not_4 (not_4_out, E);
  and and_1 (and_1_out, not_1_out, D);
  and and_2 (and_2_out, and_3_out, D);
  and and_3 (and_3_out, B, not_2_out);
  and and_4 (and_4_out, C, not_3_out);
  and and_5 (and_5_out, and_4_out, not_4_out);
  or or_1 (or_1_out, and_1_out, and_2_out);
  or or_2 (or_2_out, or_1_out, and_5_out);
  // Probe on or_2_out
endmodule
