// Logisim project BB practise skeleton.circ as structural Verilog
module Q1 (
  input  A,
  input  B,
  input  C,
  output Out
);

  wire anbnc_out, and_1_out, b_prime_or_c_out, not_1_out, not_2_out, or_1_out;

  and and_1 (and_1_out, A, B);
  and anbnc (anbnc_out, and_1_out, C);
  not not_1 (not_1_out, B);
  or b_prime_or_c (b_prime_or_c_out, not_1_out, C);
  or or_1 (or_1_out, anbnc_out, b_prime_or_c_out);
  not not_2 (not_2_out, A);
  or or_2 (Out, or_1_out, not_2_out);
endmodule

module Q2 (
  input  A,
  input  B,
  input  C,
  input  D,
  output Out
);

  wire and_1_out, and_2_out, nand_1_out, not_1_out;

  not not_1 (not_1_out, A);
  and and_1 (and_1_out, A, C);
  nand nand_1 (nand_1_out, B, D);
  and and_2 (and_2_out, and_1_out, nand_1_out);
  or or_1 (Out, not_1_out, and_2_out);
endmodule

module Q3 (
  input  D,
  input  Clk,
  output Q,
  output Q_prime
);

  wire nand_1_out, nand_2_out, nand_3_out, nand_4_out, nand_5_out, nand_6_out, nand_7_out, nand_8_out,
       nand_9_out, nand_10_out;

  nand nand_1 (nand_1_out, Clk, Clk);
  nand nand_2 (nand_2_out, D, nand_1_out);
  nand nand_3 (nand_3_out, nand_1_out, nand_4_out);
  nand nand_4 (nand_4_out, D, D);
  nand nand_5 (nand_5_out, nand_1_out, nand_1_out);
  nand nand_6 (nand_6_out, nand_2_out, nand_7_out);
  nand nand_7 (nand_7_out, nand_6_out, nand_3_out);
  nand nand_8 (nand_8_out, nand_6_out, nand_6_out);
  nand nand_9 (nand_9_out, nand_6_out, nand_5_out);
  nand nand_10 (nand_10_out, nand_5_out, nand_8_out);
  nand nand_11 (Q, nand_9_out, Q_prime);
  nand nand_12 (Q_prime, Q, nand_10_out);
endmodule

module Q4 (
  output [7:0] out,
  output [4:0] out_2
);

  wire clock_1_out, in_out, not_1_out, register_1_q;

  Button in (.out(in_out));
  Clock clock_1 (.out(clock_1_out));
  Counter #(.width(5), .max('h1f)) counter_1 (
    .D(5'b00001), .count(in_out), .Q(out_2), .clk(clock_1_out), .clr(not_1_out));  // open: load, carry
  not not_1 (not_1_out, register_1_q);
  Register #(.width(1)) register_1 (.D(in_out), .Q(register_1_q), .clk(clock_1_out));  // open: en, clr
  RAM #(.addrWidth(6), .bus("separate")) ram_1 (
    .addr({1'b0, out_2}), .data(out), .str(1'b0), .clk(clock_1_out), .ld(1'b1));  // open: din, sel, clr
endmodule
