// Logisim project 1.11_karnaugh_implementation_NAND.circ as structural Verilog: 1 circuit, main circuit main
module main (
  input  A,
  input  B,
  input  C,
  input  D,
  input  E
);

  wire nand_1_out, nand_2_out, nand_3_out, nand_4_out, nand_5_out, nand_6_out, nand_7_out, nand_8_out,
       nand_9_out, nand_10_out, nand_11_out;

  nand nand_1 (nand_1_out, A, A);
  nand nand_2 (nand_2_out, C, C);
  nand nand_3 (nand_3_out, D, D);
  nand nand_4 (nand_4_out, E, E);
  nand nand_5 (nand_5_out, B, D);
  nand nand_6 (nand_6_out, nand_3_out, nand_4_out);
  nand nand_7 (nand_7_out, nand_1_out, D);
  nand nand_8 (nand_8_out, nand_5_out, nand_2_out);
  nand nand_9 (nand_9_out, nand_6_out, C);
  nand nand_10 (nand_10_out, nand_8_out, nand_8_out, nand_9_out);
  nand nand_11 (nand_11_out, nand_7_out, nand_10_out);
  // Probe on nand_11_out
endmodule
