// Logisim project 1.12_1.19_and_1.11_combined.circ as structural Verilog: 1 circuit, main circuit main
module main (
  input  A,
  input  B,
  input  C,
  input  D,
  input  E
);

  wire and_1_out, and_2_out, and_3_out, and_4_out, and_5_out, nand_1_out, nand_2_out, nand_3_out, nand_4_out,
       nand_5_out, nand_6_out, nand_7_out, nand_8_out, nand_9_out, nand_10_out, nand_11_out, not_1_out,
       not_2_out, not_3_out, not_4_out, or_1_out, or_2_out;

  not not_1 (not_1_out, A);
  not not_2 (not_2_out, C);
  not not_3 (not_3_out, D);
  not not_4 (not_4_out, E);
  nand nand_1 (nand_1_out, A, A);
  nand nand_2 (nand_2_out, C, C);
  nand nand_3 (nand_3_out, D, D);
  nand nand_4 (nand_4_out, E, E);
  and and_1 (and_1_out, not_1_out, D);
  and and_2 (and_2_out, B, not_2_out);
  and and_3 (and_3_out, C, not_3_out);
  nand nand_5 (nand_5_out, B, D);
  nand nand_6 (nand_6_out, nand_3_out, nand_4_out);
  and and_4 (and_4_out, and_2_out, D);
  and and_5 (and_5_out, and_3_out, not_4_out);
  nand nand_7 (nand_7_out, nand_1_out, D);
  nand nand_8 (nand_8_out, nand_5_out, nand_2_out);
  nand nand_9 (nand_9_out, nand_6_out, C);
  nand nand_10 (nand_10_out, nand_8_out, nand_8_out, nand_9_out);
  or or_1 (or_1_out, and_1_out, and_4_out);
  nand nand_11 (nand_11_out, nand_7_out, nand_10_out);
  or or_2 (or_2_out, or_1_out, and_5_out);
  // Probe on nand_11_out
  // Probe on or_2_out
endmodule
