// Logisim project 1.5_XOR-NAND.circ as structural Verilog: 1 circuit, main circuit main
module main (
  input  in_1,
  input  in_2
);

  wire nand_1_out, nand_2_out, nand_3_out, nand_4_out, nand_5_out, xor_1_out;

  xor xor_1 (xor_1_out, in_1, in_2);
  // Probe on xor_1_out
  nand nand_1 (nand_1_out, in_1, in_1);
  nand nand_2 (nand_2_out, in_2, in_2);
  nand nand_3 (nand_3_out, nand_1_out, in_2);
  nand nand_4 (nand_4_out, in_1, nand_2_out);
  nand nand_5 (nand_5_out, nand_3_out, nand_4_out);
  // Probe on nand_5_out
endmodule
