// Logisim project class_exercise.circ as structural Verilog: 1 circuit, main circuit main
module main (
  input  A,
  input  B,
  input  C,
  input  D
);

  wire A___B_out, A__BB_out, A_A_out, AB___AB_out, and_1_out, and_2_out, and_3_out, and_4_out, B___B_out,
       B__AA____A__BB_out, B__AA_out, C___C_out, C__DD____D__CC_out, C__DD_out, C_D_out, CD___CD_out,
       D__CC_out, D_D_out, nand_1_out, O1_out, O2_out, or_1_out, xor_1_out, xor_2_out;

  and and_1 (and_1_out, B, A);
  xor xor_1 (xor_1_out, A, B);
  and and_2 (and_2_out, C, D);
  xor xor_2 (xor_2_out, C, D);
  and and_3 (and_3_out, xor_1_out, and_2_out);
  and and_4 (and_4_out, and_1_out, xor_2_out);
  // Probe on or_1_out
  or or_1 (or_1_out, and_3_out, and_4_out);
  nand A_A (A_A_out, A, A);
  nand A___B (A___B_out, A, B);
  nand B___B (B___B_out, B, B);
  nand C___C (C___C_out, C, C);
  nand C_D (C_D_out, C, D);
  not D_D (D_D_out, D);  // NAND_Gate
  nand B__AA (B__AA_out, A_A_out, B);
  nand AB___AB (AB___AB_out, A___B_out, A___B_out);
  nand A__BB (A__BB_out, A, B___B_out);
  not CD___CD (CD___CD_out, C_D_out);  // NAND_Gate
  nand D__CC (D__CC_out, C___C_out, D);
  nand C__DD (C__DD_out, C, D_D_out);
  nand B__AA____A__BB (B__AA____A__BB_out, B__AA_out, A__BB_out);
  nand C__DD____D__CC (C__DD____D__CC_out, D__CC_out, C__DD_out);
  nand O2 (O2_out, B__AA____A__BB_out, CD___CD_out);
  nand O1 (O1_out, AB___AB_out, C__DD____D__CC_out);
  nand nand_1 (nand_1_out, O2_out, O1_out);
  // Probe on nand_1_out
endmodule
