// Logisim project 1.1_half_adder.circ as structural Verilog: 1 circuit, main circuit main
module main (
  input  A,
  input  B
);

  wire and_1_out, xor_1_out;

  // Probe on xor_1_out
  xor xor_1 (xor_1_out, A, B);
  // Probe on and_1_out
  and and_1 (and_1_out, A, B);
endmodule
