// Logisim project 1.2_incrementer.circ as structural Verilog: 2 circuits, main circuit 4 bit incrementer
module _4_bit_incrementer (
  input  A_1,
  input  A_2,
  input  A_3,
  input  A_0
);

  wire and_1_out, and_2_out, and_3_out, and_4_out, xor_1_out, xor_2_out, xor_3_out, xor_4_out;

  // Probe on xor_1_out
  xor xor_1 (xor_1_out, A_0, 1'b1);
  and and_1 (and_1_out, A_0, 1'b1);
  // Probe on xor_2_out
  xor xor_2 (xor_2_out, A_1, and_1_out);
  and and_2 (and_2_out, and_1_out, A_1);
  xor xor_3 (xor_3_out, A_2, and_2_out);
  and and_3 (and_3_out, and_2_out, A_2);
  // Probe on xor_3_out
  // Probe on xor_4_out
  xor xor_4 (xor_4_out, A_3, and_3_out);
  and and_4 (and_4_out, and_3_out, A_3);
  // Probe on and_4_out

  // Notes on the sheet:
  //   Basically the point of an adder is to take a given 4-bit number which is defined by A_0 to A_3 and add 1 to it
endmodule

module half_adder (
  input  A,
  input  C_in,
  output S,
  output C_out
);

  xor xor_1 (S, A, C_in);
  and and_1 (C_out, C_in, A);
endmodule
