// Logisim project 1.3_incrementer_splitter.circ as structural Verilog: 1 circuit, main circuit main
module main (
  input  [3:0] in_1
);

  wire and_1_out, and_2_out, and_3_out, and_4_out;
  wire [3:0] xor_1_out;

  xor xor_1 (xor_1_out[0], in_1[0], 1'b1);
  and and_1 (and_1_out, in_1[0], 1'b1);
  // Probe on xor_1_out
  xor xor_2 (xor_1_out[1], in_1[1], and_1_out);
  and and_2 (and_2_out, and_1_out, in_1[1]);
  xor xor_3 (xor_1_out[2], in_1[2], and_2_out);
  and and_3 (and_3_out, and_2_out, in_1[2]);
  xor xor_4 (xor_1_out[3], in_1[3], and_3_out);
  // Probe on and_4_out
  and and_4 (and_4_out, and_3_out, in_1[3]);
endmodule
