// Logisim project 2.1_1bit_full_adder.circ as structural Verilog: 1 circuit, main circuit main
module main (
  input  A,
  input  B,
  input  C_in
);

  wire and_1_out, and_2_out, Needed_configuring_out, or_1_out, xor_1_out;

  xor Needed_configuring (Needed_configuring_out, A, B, C_in);
  and and_1 (and_1_out, A, B);
  xor xor_1 (xor_1_out, A, B);
  // Probe on Needed_configuring_out
  and and_2 (and_2_out, xor_1_out, C_in);
  or or_1 (or_1_out, and_1_out, and_2_out);
  // Probe on or_1_out
endmodule
