// Logisim project 2.2_2.3_4bit_adder.circ as structural Verilog: 3 circuits, main circuit main
module main (
  input  [3:0] A,
  input  [3:0] B
);

  wire n1bit_full_adder_1_c_out, n1bit_full_adder_2_c_out, n1bit_full_adder_3_c_out, n1bit_full_adder_4_c_out;
  wire [3:0] n1bit_full_adder_1_s;

  // Probe on n1bit_full_adder_4_c_out
  // Probe on n1bit_full_adder_1_s
  _1bit_full_adder u_1bit_full_adder_1 (
    .C_in(1'b0), .S(n1bit_full_adder_1_s[0]), .A(A[0]), .B(B[0]), .C_out(n1bit_full_adder_1_c_out));
  _1bit_full_adder u_1bit_full_adder_2 (
    .C_in(n1bit_full_adder_1_c_out), .S(n1bit_full_adder_1_s[1]), .A(A[1]), .B(B[1]),
    .C_out(n1bit_full_adder_2_c_out));
  _1bit_full_adder u_1bit_full_adder_3 (
    .C_in(n1bit_full_adder_2_c_out), .S(n1bit_full_adder_1_s[2]), .A(A[2]), .B(B[2]),
    .C_out(n1bit_full_adder_3_c_out));
  _1bit_full_adder u_1bit_full_adder_4 (
    .C_in(n1bit_full_adder_3_c_out), .S(n1bit_full_adder_1_s[3]), .A(A[3]), .B(B[3]),
    .C_out(n1bit_full_adder_4_c_out));
endmodule

module _1bit_full_adder (
  input  C_in,
  input  A,
  input  B,
  output S,
  output C_out
);

  wire and_1_out, and_2_out, xor_1_out;

  xor Needed_configuring (S, A, B, C_in);
  and and_1 (and_1_out, A, B);
  xor xor_1 (xor_1_out, A, B);
  and and_2 (and_2_out, xor_1_out, C_in);
  or or_1 (C_out, and_1_out, and_2_out);
endmodule

module _4bit_incrementer (
  input  [3:0] A
);

  wire and_1_out, and_2_out, and_3_out, and_4_out;
  wire [3:0] xor_1_out;

  xor xor_1 (xor_1_out[0], A[0], 1'b1);
  and and_1 (and_1_out, A[0], 1'b1);
  // Probe on and_4_out
  // Probe on xor_1_out
  xor xor_2 (xor_1_out[1], A[1], and_1_out);
  and and_2 (and_2_out, and_1_out, A[1]);
  xor xor_3 (xor_1_out[2], A[2], and_2_out);
  and and_3 (and_3_out, and_2_out, A[2]);
  xor xor_4 (xor_1_out[3], A[3], and_3_out);
  and and_4 (and_4_out, and_3_out, A[3]);
endmodule
