// Logisim project 3.1_half_adder_NAND.circ as structural Verilog: 4 circuits, main circuit main
module main (
  input  A,
  input  B,
  output S,
  output C,
  output S_2,
  output C_2,
  output S_3,
  output C_3
);

  original Original (.A(A), .B(B), .S(S), .C(C));
  NAND_implementation _7_NANDs (.A(A), .B(B), .S(S_2), .C(C_2));
  _5_NAND_Implementation _5_NANDs (.A(A), .B(B), .S(S_3), .C_out(C_3));
endmodule

module original (
  input  A,
  input  B,
  output S,
  output C
);

  xor xor_1 (S, A, B);
  and and_1 (C, A, B);
endmodule

module NAND_implementation (
  input  A,
  input  B,
  output S,
  output C
);

  wire A__BB_out, A_A_out, A_B_out, B__AA_out, B_B_out;

  nand A_B (A_B_out, B, A);
  nand A_A (A_A_out, A, A);
  nand B_B (B_B_out, B, B);
  not AB___AB (C, A_B_out);  // NAND_Gate
  nand A__BB (A__BB_out, A, B_B_out);
  nand B__AA (B__AA_out, A_A_out, B);
  nand nand_1 (S, A__BB_out, B__AA_out);
endmodule

module _5_NAND_Implementation (
  input  A,
  input  B,
  output S,
  output C_out
);

  wire A__AB_out, AB_out, B__AB_out;

  nand AB (AB_out, A, B);
  nand A__AB (A__AB_out, A, AB_out);
  nand B__AB (B__AB_out, AB_out, B);
  nand AB___AB (C_out, AB_out, AB_out);
  nand nand_1 (S, A__AB_out, B__AB_out);
endmodule
