// Logisim project 3.2_full_adder_NAND.circ as structural Verilog: 3 circuits, main circuit main
module main (
  input  A,
  input  B,
  input  C_in,
  output S,
  output C_out,
  output C_out_2,
  output S_2
);

  original original_1 (.A(A), .B(B), .C_in(C_in), .S(S), .C_out(C_out));
  NAND_implementation nand_implementation_1 (.A(A), .B(B), .C_in(C_in), .C_out(C_out_2), .S(S_2));
endmodule

module original (
  input  A,
  input  B,
  input  C_in,
  output S,
  output C_out
);

  wire and_1_out, and_2_out, xor_1_out;

  xor Needed_configuring (S, A, B, C_in);
  and and_1 (and_1_out, A, B);
  xor xor_1 (xor_1_out, A, B);
  and and_2 (and_2_out, xor_1_out, C_in);
  or or_1 (C_out, and_1_out, and_2_out);
endmodule

module NAND_implementation (
  input  A,
  input  B,
  input  C_in,
  output C_out,
  output S
);

  wire A__BB_out, A_A_out, A_B_out, B__AA_out, B_B_out, C_____x_out, C__x_x_out, C_C__x_out, C_C_out,
       x____B__AA____A__BB_out, x_x_out;

  nand A_B (A_B_out, B, A);
  nand A_A (A_A_out, A, A);
  nand B_B (B_B_out, B, B);
  nand C_C (C_C_out, C_in, C_in);
  nand B__AA (B__AA_out, A_A_out, B);
  nand A__BB (A__BB_out, A, B_B_out);
  nand x____B__AA____A__BB (x____B__AA____A__BB_out, B__AA_out, A__BB_out);
  nand C_____x (C_____x_out, x____B__AA____A__BB_out, C_in);
  nand x_x (x_x_out, x____B__AA____A__BB_out, x____B__AA____A__BB_out);
  nand nand_1 (C_out, A_B_out, C_____x_out);
  nand C_C__x (C_C__x_out, x____B__AA____A__BB_out, C_C_out);
  nand C__x_x (C__x_x_out, x_x_out, C_in);
  nand nand_2 (S, C_C__x_out, C__x_x_out);
endmodule
