// Logisim project 4.1_4.2_multiplexer_demultiplexer.circ as structural Verilog: 1 circuit, main circuit main
module main (
  input  [3:0] A,
  input  [3:0] B,
  input  [1:0] in_3,
  input  E,
  input  D,
  output [3:0] out_6
);

  wire demultiplexer_1_out0;
  wire [3:0] and_1_out, nor_1_out, or_1_out, xor_1_out;

  assign and_1_out = A & B;  // AND_Gate and_1, 4 bits wide
  assign or_1_out = A | B;  // OR_Gate or_1, 4 bits wide
  assign nor_1_out = ~(A | B);  // NOR_Gate nor_1, 4 bits wide
  assign xor_1_out = A ^ B;  // XOR_Gate xor_1, 4 bits wide
  Multiplexer #(.select(2), .width(4)) multiplexer_1 (
    .in0(and_1_out), .in1(or_1_out), .in2(nor_1_out), .in3(xor_1_out), .out(out_6), .sel(in_3),
    .en(demultiplexer_1_out0));
  Demultiplexer demultiplexer_1 (.out0(demultiplexer_1_out0), .in(E), .sel(D));  // open: out1, en
endmodule
