// Logisim project 5_ALU.circ as structural Verilog: 3 circuits, main circuit main
module main (
  input  [3:0] y,
  input  zy,
  input  ny,
  input  [3:0] x,
  input  zx,
  input  nx,
  input  f,
  input  no,
  output Overflow_Error,
  output [3:0] out_10
);

  wire [3:0] and_1_out, full_4_bit_adder_1_out, multiplexer_1_out, multiplexer_2_out, multiplexer_3_out,
       multiplexer_4_out, multiplexer_5_out, not_1_out, not_2_out, not_3_out, not_4_out, not_5_out;

  Multiplexer #(.width(4), .enable("false")) multiplexer_1 (
    .in0(y), .in1(not_1_out), .out(multiplexer_1_out), .sel(zy));
  assign not_1_out = ~4'b1111;  // NOT_Gate not_1, 4 bits wide
  Multiplexer #(.width(4), .enable("false")) multiplexer_2 (
    .in0(x), .in1(not_2_out), .out(multiplexer_2_out), .sel(zx));
  assign not_2_out = ~4'b1111;  // NOT_Gate not_2, 4 bits wide
  assign not_3_out = ~multiplexer_1_out;  // NOT_Gate not_3, 4 bits wide
  assign not_4_out = ~multiplexer_2_out;  // NOT_Gate not_4, 4 bits wide
  Multiplexer #(.width(4), .enable("false")) multiplexer_3 (
    .in0(multiplexer_1_out), .in1(not_3_out), .out(multiplexer_3_out), .sel(ny));
  Multiplexer #(.width(4), .enable("false")) multiplexer_4 (
    .in0(multiplexer_2_out), .in1(not_4_out), .out(multiplexer_4_out), .sel(nx));
  Full_4_bit_adder full_4_bit_adder_1 (
    .Out(full_4_bit_adder_1_out), .C(Overflow_Error), .X(multiplexer_4_out), .Y(multiplexer_3_out));
  assign and_1_out = multiplexer_3_out & multiplexer_4_out;  // AND_Gate and_1, 4 bits wide
  Multiplexer #(.width(4), .enable("false")) multiplexer_5 (
    .in0(and_1_out), .in1(full_4_bit_adder_1_out), .out(multiplexer_5_out), .sel(f));
  assign not_5_out = ~multiplexer_5_out;  // NOT_Gate not_5, 4 bits wide
  Multiplexer #(.width(4), .enable("false")) multiplexer_6 (
    .in0(multiplexer_5_out), .in1(not_5_out), .out(out_10), .sel(no));
endmodule

module Full_Adder_Unit (
  input  A,
  input  B,
  input  C_in,
  output S,
  output C_out
);

  wire A__BB_out, A_A_out, A_B_out, B__AA_out, B_B_out, C_____x_out, C__x_x_out, C_C__x_out, C_C_out,
       x____B__AA____A__BB_out, x_x_out;

  nand A_B (A_B_out, B, A);
  nand A_A (A_A_out, A, A);
  nand B_B (B_B_out, B, B);
  nand C_C (C_C_out, C_in, C_in);
  nand B__AA (B__AA_out, A_A_out, B);
  nand A__BB (A__BB_out, A, B_B_out);
  nand x____B__AA____A__BB (x____B__AA____A__BB_out, B__AA_out, A__BB_out);
  nand C_____x (C_____x_out, x____B__AA____A__BB_out, C_in);
  nand x_x (x_x_out, x____B__AA____A__BB_out, x____B__AA____A__BB_out);
  nand nand_1 (C_out, A_B_out, C_____x_out);
  nand C_C__x (C_C__x_out, x____B__AA____A__BB_out, C_C_out);
  nand C__x_x (C__x_x_out, x_x_out, C_in);
  nand nand_2 (S, C_C__x_out, C__x_x_out);
endmodule

module Full_4_bit_adder (
  input  [3:0] X,
  input  [3:0] Y,
  output C,
  output [3:0] Out
);

  wire full_adder_unit_1_c_out, full_adder_unit_2_c_out, full_adder_unit_3_c_out, not_1_out;

  not not_1 (not_1_out, 1'b1);
  Full_Adder_Unit full_adder_unit_1 (.A(X[0]), .B(Y[0]), .C_in(not_1_out), .S(Out[0]), .C_out(full_adder_unit_1_c_out));
  Full_Adder_Unit full_adder_unit_2 (
    .A(X[2]), .B(Y[2]), .C_in(full_adder_unit_3_c_out), .S(Out[2]), .C_out(full_adder_unit_2_c_out));
  Full_Adder_Unit full_adder_unit_3 (
    .A(X[1]), .B(Y[1]), .C_in(full_adder_unit_1_c_out), .S(Out[1]), .C_out(full_adder_unit_3_c_out));
  Full_Adder_Unit full_adder_unit_4 (.A(X[3]), .B(Y[3]), .C_in(full_adder_unit_2_c_out), .S(Out[3]), .C_out(C));
endmodule
