// Logisim project 7 segment counter.circ as structural Verilog
module Middle_Top (
  input  a__2_3,
  input  b__2_2,
  input  c__2_1,
  input  d__2_0,
  output out_5
);

  wire and_1_out, and_2_out, and_3_out, and_4_out, and_5_out, and_6_out, not_1_out, not_2_out, not_3_out,
       not_4_out;

  not not_1 (not_1_out, a__2_3);
  not not_2 (not_2_out, b__2_2);
  not not_3 (not_3_out, c__2_1);
  not not_4 (not_4_out, d__2_0);
  and and_1 (and_1_out, a__2_3, not_2_out, not_3_out);
  and and_2 (and_2_out, a__2_3, not_3_out, not_4_out);
  and and_3 (and_3_out, not_1_out, b__2_2, d__2_0);
  and and_4 (and_4_out, not_2_out, not_4_out);
  and and_5 (and_5_out, b__2_2, c__2_1);
  and and_6 (and_6_out, not_1_out, c__2_1);
  or or_1 (out_5, and_1_out, and_2_out, and_3_out, and_4_out, and_5_out, and_6_out);
endmodule

module Right_Top (
  input  a__2_3,
  input  b__2_2,
  input  c__2_1,
  input  d__2_0,
  output out_5
);

  wire and_1_out, and_2_out, and_3_out, and_4_out, and_5_out, not_1_out, not_2_out, not_3_out, not_4_out;

  not not_1 (not_1_out, a__2_3);
  not not_2 (not_2_out, b__2_2);
  not not_3 (not_3_out, c__2_1);
  not not_4 (not_4_out, d__2_0);
  and and_1 (and_1_out, a__2_3, not_2_out, not_3_out, not_4_out);
  and and_2 (and_2_out, not_1_out, not_2_out);
  and and_3 (and_3_out, a__2_3, not_2_out, c__2_1, d__2_0);
  and and_4 (and_4_out, a__2_3, not_3_out, d__2_0);
  and and_5 (and_5_out, a__2_3, not_2_out, not_4_out);
  or or_1 (out_5, and_1_out, and_2_out, and_3_out, and_4_out, and_5_out);
endmodule
