// Logisim project D-Latch.circ as structural Verilog
module R_S_Latch__active_high (
  input  S_prime,
  input  R_prime,
  output Q,
  output Q_prime
);

  nand nand_1 (Q, S_prime, Q_prime);
  nand nand_2 (Q_prime, Q, R_prime);
endmodule

module D_Latch_Extension (
  input  en,
  input  D,
  output S_prime,
  output R_prime
);

  wire not_1_out;

  not not_1 (not_1_out, D);
  nand nand_1 (S_prime, en, D);
  nand nand_2 (R_prime, not_1_out, en);
endmodule
