// Logisim project Pos and Neg D Flip flops.circ as structural Verilog
module R_S_Latch (
  input  S_prime,
  input  R_prime,
  output Q,
  output Q_prime
);

  nand nand_1 (Q, S_prime, Q_prime);
  nand nand_2 (Q_prime, Q, R_prime);

  // Notes on the sheet:
  //   Active low
  //   1 = OFF
  //   They shouldn't both be on
endmodule

module D_Latch_Extension (
  input  D,
  input  en,
  output Q,
  output Q_prime
);

  wire nand_1_out, nand_2_out, not_1_out;

  nand nand_1 (nand_1_out, D, en);
  nand nand_2 (nand_2_out, en, not_1_out);
  not not_1 (not_1_out, D);
  R_S_Latch r_s_latch_1 (.S_prime(nand_1_out), .R_prime(nand_2_out), .Q(Q), .Q_prime(Q_prime));
endmodule

module Negative_D_Flip_flop (
  input  D,
  input  en,
  output Q,
  output Q_prime
);

  wire d_latch_extension_2_q, not_1_out;

  D_Latch_Extension d_latch_extension_1 (.D(d_latch_extension_2_q), .en(not_1_out), .Q(Q), .Q_prime(Q_prime));
  D_Latch_Extension d_latch_extension_2 (.D(D), .en(en), .Q(d_latch_extension_2_q));  // open: Q_prime
  not not_1 (not_1_out, en);
endmodule

module Positive_D_Flip_flop (
  input  in_1,
  input  in_2,
  output Q,
  output Q_prime
);

  wire not_1_out;

  Negative_D_Flip_flop negative_d_flip_flop_1 (.D(in_1), .en(not_1_out), .Q(Q), .Q_prime(Q_prime));
  not not_1 (not_1_out, in_2);
endmodule
