// Logisim project 1_program_counter.circ as structural Verilog: 1 circuit, main circuit main
module main (
  input  [15:0] in,
  input  inc,
  input  load,
  input  reset,
  output [15:0] out_5
);

  wire clock_1_out;
  wire [15:0] adder_1_out, multiplexer_1_out, multiplexer_2_out, multiplexer_3_out;

  Multiplexer #(.width(16)) multiplexer_1 (
    .in0({16{1'b0}}), .in1(adder_1_out), .out(multiplexer_1_out), .sel(inc));  // open: en
  Multiplexer #(.width(16)) multiplexer_2 (
    .in0(multiplexer_1_out), .in1(in), .out(multiplexer_2_out), .sel(load));  // open: en
  Multiplexer #(.width(16)) multiplexer_3 (
    .in0(multiplexer_2_out), .in1({16{1'b0}}), .out(multiplexer_3_out), .sel(reset));  // open: en
  Register #(.width(16)) register_1 (.D(multiplexer_3_out), .Q(out_5), .clk(clock_1_out));  // open: en, clr
  Clock clock_1 (.out(clock_1_out));
  Adder #(.width(16)) adder_1 (.a(out_5), .b(16'h1), .out(adder_1_out));  // open: cin, cout
endmodule
