// Logisim project 8-word RAM.circ as structural Verilog
module RAM (
  input  [15:0] in,
  input  [2:0] address,
  input  in_3,
  output [15:0] out_4
);

  wire clock_1_out;
  wire [7:0] demultiplexer_1_out7;
  wire [15:0] demultiplexer_2_out0, demultiplexer_2_out1, demultiplexer_2_out2, demultiplexer_2_out3,
       demultiplexer_2_out4, demultiplexer_2_out5, demultiplexer_2_out6, demultiplexer_2_out7,
       multiplexer_1_out, multiplexer_2_out, multiplexer_3_out, multiplexer_4_out, multiplexer_5_out,
       multiplexer_6_out, multiplexer_7_out, multiplexer_8_out, register_1_q, register_2_q, register_3_q,
       register_4_q, register_5_q, register_6_q, register_7_q, register_8_q;

  Demultiplexer #(.select(3)) demultiplexer_1 (
    .out0(demultiplexer_1_out7[7]), .out1(demultiplexer_1_out7[6]), .out2(demultiplexer_1_out7[5]),
    .out3(demultiplexer_1_out7[4]), .out4(demultiplexer_1_out7[3]), .out5(demultiplexer_1_out7[2]),
    .out6(demultiplexer_1_out7[1]), .out7(demultiplexer_1_out7[0]), .in(in_3), .sel(address));  // open: en
  Demultiplexer #(.select(3), .width(16)) demultiplexer_2 (
    .out0(demultiplexer_2_out0), .out1(demultiplexer_2_out1), .out2(demultiplexer_2_out2),
    .out3(demultiplexer_2_out3), .out4(demultiplexer_2_out4), .out5(demultiplexer_2_out5),
    .out6(demultiplexer_2_out6), .out7(demultiplexer_2_out7), .in(in), .sel(address));  // open: en
  Multiplexer #(.width(16)) multiplexer_1 (
    .in0(register_1_q), .in1(demultiplexer_2_out0), .out(multiplexer_1_out), .sel(demultiplexer_1_out7[7]));  // open: en
  Register #(.width(16)) register_1 (.D(multiplexer_1_out), .Q(register_1_q), .clk(clock_1_out));  // open: en, clr
  Multiplexer #(.width(16)) multiplexer_2 (
    .in0(register_2_q), .in1(demultiplexer_2_out1), .out(multiplexer_2_out), .sel(demultiplexer_1_out7[6]));  // open: en
  Register #(.width(16)) register_2 (.D(multiplexer_2_out), .Q(register_2_q), .clk(clock_1_out));  // open: en, clr
  Register #(.width(16)) register_3 (.D(multiplexer_3_out), .Q(register_3_q), .clk(clock_1_out));  // open: en, clr
  Multiplexer #(.width(16)) multiplexer_3 (
    .in0(register_3_q), .in1(demultiplexer_2_out2), .out(multiplexer_3_out), .sel(demultiplexer_1_out7[5]));  // open: en
  Multiplexer #(.width(16)) multiplexer_4 (
    .in0(register_4_q), .in1(demultiplexer_2_out3), .out(multiplexer_4_out), .sel(demultiplexer_1_out7[4]));  // open: en
  Register #(.width(16)) register_4 (.D(multiplexer_4_out), .Q(register_4_q), .clk(clock_1_out));  // open: en, clr
  Register #(.width(16)) register_5 (.D(multiplexer_5_out), .Q(register_5_q), .clk(clock_1_out));  // open: en, clr
  Multiplexer #(.width(16)) multiplexer_5 (
    .in0(register_5_q), .in1(demultiplexer_2_out4), .out(multiplexer_5_out), .sel(demultiplexer_1_out7[3]));  // open: en
  Multiplexer #(.width(16)) multiplexer_6 (
    .in0(register_6_q), .in1(demultiplexer_2_out5), .out(multiplexer_6_out), .sel(demultiplexer_1_out7[2]));  // open: en
  Register #(.width(16)) register_6 (.D(multiplexer_6_out), .Q(register_6_q), .clk(clock_1_out));  // open: en, clr
  Multiplexer #(.width(16)) multiplexer_7 (
    .in0(register_7_q), .in1(demultiplexer_2_out6), .out(multiplexer_7_out), .sel(demultiplexer_1_out7[1]));  // open: en
  Register #(.width(16)) register_7 (.D(multiplexer_7_out), .Q(register_7_q), .clk(clock_1_out));  // open: en, clr
  Multiplexer #(.width(16)) multiplexer_8 (
    .in0(register_8_q), .in1(demultiplexer_2_out7), .out(multiplexer_8_out), .sel(demultiplexer_1_out7[0]));  // open: en
  Register #(.width(16)) register_8 (.D(multiplexer_8_out), .Q(register_8_q), .clk(clock_1_out));  // open: en, clr
  Clock clock_1 (.out(clock_1_out));
  Multiplexer #(.select(3), .width(16)) multiplexer_9 (
    .in0(register_1_q), .in1(register_2_q), .in2(register_3_q), .in3(register_4_q), .in4(register_5_q),
    .in5(register_6_q), .in6(register_7_q), .in7(register_8_q), .out(out_4), .sel(address));  // open: en
endmodule
