// Logisim project Circuit Practice.circ as structural Verilog
module half_adder (
  input  a,
  input  b,
  output S,
  output C_out
);

  xor xor_1 (S, a, b);
  and and_1 (C_out, a, b);
endmodule

module full_adder__1bit (
  input  a,
  input  b,
  input  C_in,
  output S,
  output C_out
);

  wire and_1_out, and_2_out, xor_1_out;

  xor xor_1 (xor_1_out, a, b);
  and and_1 (and_1_out, a, b);
  xor xor_2 (S, xor_1_out, C_in);
  and and_2 (and_2_out, xor_1_out, C_in);
  or or_1 (C_out, and_2_out, and_1_out);
endmodule

module R_S_Latch (
  input  S_prime,
  input  R_prime,
  output Q,
  output Q_prime
);

  nand nand_1 (Q, S_prime, Q_prime);
  nand nand_2 (Q_prime, Q, R_prime);
endmodule

module D_Latch (
  input  D,
  input  en,
  output Q,
  output Q_prime
);

  wire nand_1_out, nand_2_out, not_1_out;

  not not_1 (not_1_out, D);
  nand nand_1 (nand_1_out, D, en);
  R_S_Latch r_s_latch_1 (.S_prime(nand_1_out), .R_prime(nand_2_out), .Q(Q), .Q_prime(Q_prime));
  nand nand_2 (nand_2_out, en, not_1_out);
endmodule

module D_Flip_Flop__NET (
  input  D,
  input  en,
  output Q,
  output Q_prime
);

  wire d_latch_1_q, not_1_out;

  D_Latch d_latch_1 (.D(D), .en(en), .Q(d_latch_1_q));  // open: Q_prime
  not not_1 (not_1_out, en);
  D_Latch d_latch_2 (.D(d_latch_1_q), .en(not_1_out), .Q(Q), .Q_prime(Q_prime));
endmodule

module D_Flip_Flop__PET (
  input  D,
  input  en,
  output Q,
  output Q_prime
);

  wire not_1_out;

  not not_1 (not_1_out, en);
  D_Flip_Flop__NET d_flip_flop_net_1 (.D(D), .en(not_1_out), .Q(Q), .Q_prime(Q_prime));
endmodule

// Reg
module Register__1bit (
  input  in,
  input  CLK,
  input  load,
  output Q,
  output Q_prime
);

  wire multiplexer_1_out;

  Multiplexer multiplexer_1 (.in0(Q), .in1(in), .out(multiplexer_1_out), .sel(load));  // open: en
  D_Flip_Flop__PET DFF (.D(multiplexer_1_out), .en(CLK), .Q(Q), .Q_prime(Q_prime));
endmodule

module Register__8bit (
  input  [7:0] in,
  input  load,
  input  CLK,
  output [7:0] out
);

  Register__1bit _0 (.in(in[0]), .CLK(CLK), .load(load), .Q(out[0]));  // open: Q_prime
  Register__1bit _1 (.in(in[1]), .CLK(CLK), .load(load), .Q(out[1]));  // open: Q_prime
  Register__1bit _2 (.in(in[2]), .CLK(CLK), .load(load), .Q(out[2]));  // open: Q_prime
  Register__1bit _3 (.in(in[3]), .CLK(CLK), .load(load), .Q(out[3]));  // open: Q_prime
  Register__1bit _4 (.in(in[4]), .CLK(CLK), .load(load), .Q(out[4]));  // open: Q_prime
  Register__1bit _5 (.in(in[5]), .CLK(CLK), .load(load), .Q(out[5]));  // open: Q_prime
  Register__1bit _6 (.in(in[6]), .CLK(CLK), .load(load), .Q(out[6]));  // open: Q_prime
  Register__1bit _7 (.in(in[7]), .CLK(CLK), .load(load), .Q(out[7]));  // open: Q_prime
endmodule

module one_shot (
  input  in,
  output out
);

  wire clock_1_out, register_1bit_1_q, register_1bit_2_q_prime;

  Register__1bit register_1bit_1 (.in(in), .CLK(clock_1_out), .load(1'b1), .Q(register_1bit_1_q));  // open: Q_prime
  Register__1bit register_1bit_2 (
    .in(register_1bit_1_q), .CLK(clock_1_out), .load(1'b1), .Q_prime(register_1bit_2_q_prime));  // open: Q
  Clock clock_1 (.out(clock_1_out));
  and and_1 (out, register_1bit_1_q, register_1bit_2_q_prime);
endmodule

module counter (
  input  reset,
  output [7:0] out
);

  wire clock_1_out;
  wire [7:0] full_adder_8bit_1_out, multiplexer_1_out;

  Multiplexer #(.width(8)) multiplexer_1 (
    .in0(full_adder_8bit_1_out), .in1({8{1'b0}}), .out(multiplexer_1_out), .sel(reset));  // open: en
  Clock clock_1 (.out(clock_1_out));
  Register__8bit register_8bit_1 (.in(multiplexer_1_out), .load(1'b1), .CLK(clock_1_out), .out(out));
  full_adder__8bit full_adder_8bit_1 (.a(out), .b(8'h1), .out(full_adder_8bit_1_out));  // open: overflow
endmodule

module full_adder__8bit (
  input  [7:0] a,
  input  [7:0] b,
  output overflow,
  output [7:0] out
);

  wire full_adder_1bit_1_c_out, full_adder_1bit_2_c_out, full_adder_1bit_3_c_out, full_adder_1bit_4_c_out,
       full_adder_1bit_5_c_out, full_adder_1bit_6_c_out, full_adder_1bit_7_c_out;

  full_adder__1bit full_adder_1bit_1 (.a(a[0]), .b(b[0]), .C_in(1'b0), .S(out[0]), .C_out(full_adder_1bit_1_c_out));
  full_adder__1bit full_adder_1bit_2 (
    .a(a[1]), .b(b[1]), .C_in(full_adder_1bit_1_c_out), .S(out[1]), .C_out(full_adder_1bit_2_c_out));
  full_adder__1bit full_adder_1bit_3 (
    .a(a[2]), .b(b[2]), .C_in(full_adder_1bit_2_c_out), .S(out[2]), .C_out(full_adder_1bit_3_c_out));
  full_adder__1bit full_adder_1bit_4 (
    .a(a[3]), .b(b[3]), .C_in(full_adder_1bit_3_c_out), .S(out[3]), .C_out(full_adder_1bit_4_c_out));
  full_adder__1bit full_adder_1bit_5 (
    .a(a[4]), .b(b[4]), .C_in(full_adder_1bit_4_c_out), .S(out[4]), .C_out(full_adder_1bit_5_c_out));
  full_adder__1bit full_adder_1bit_6 (
    .a(a[5]), .b(b[5]), .C_in(full_adder_1bit_5_c_out), .S(out[5]), .C_out(full_adder_1bit_6_c_out));
  full_adder__1bit full_adder_1bit_7 (
    .a(a[6]), .b(b[6]), .C_in(full_adder_1bit_6_c_out), .S(out[6]), .C_out(full_adder_1bit_7_c_out));
  full_adder__1bit full_adder_1bit_8 (.a(a[7]), .b(b[7]), .C_in(full_adder_1bit_7_c_out), .S(out[7]), .C_out(overflow));
endmodule
