// Logisim project Circuit Practice2.circ as structural Verilog
module half_adder (
  input  a,
  input  b,
  output SUM,
  output C
);

  xor xor_1 (SUM, a, b);
  and and_1 (C, b, a);
endmodule

module full_adder (
  input  a,
  input  b,
  input  c_in,
  output S,
  output C_out
);

  wire and_1_out, and_2_out, xor_1_out;

  xor xor_1 (xor_1_out, a, b);
  xor xor_2 (S, xor_1_out, c_in);
  and and_1 (and_1_out, xor_1_out, c_in);
  and and_2 (and_2_out, b, a);
  or or_1 (C_out, and_1_out, and_2_out);
endmodule

module RS_Latch (
  input  S_prime,
  input  R_prime,
  output Q,
  output Q_prime
);

  nand nand_1 (Q, S_prime, Q_prime);
  nand nand_2 (Q_prime, Q, R_prime);
endmodule

module D_Latch (
  input  d,
  input  en,
  output out_3,
  output out_4
);

  wire nand_1_out, nand_2_out, not_1_out;

  not not_1 (not_1_out, d);
  nand nand_1 (nand_1_out, d, en);
  nand nand_2 (nand_2_out, en, not_1_out);
  RS_Latch rs_latch_1 (.S_prime(nand_1_out), .R_prime(nand_2_out), .Q(out_3), .Q_prime(out_4));
endmodule

module Flip_Flop__Negative (
  input  D,
  input  en,
  output Q,
  output Q_prime
);

  wire d_latch_1_out_3, d_latch_1_out_4, not_1_out;

  D_Latch d_latch_1 (.d(D), .en(en), .out_3(d_latch_1_out_3), .out_4(d_latch_1_out_4));
  not not_1 (not_1_out, en);
  D_Latch d_latch_2 (.d(d_latch_1_out_3), .en(not_1_out), .out_3(Q), .out_4(Q_prime));
endmodule

module Flip_Flop__Positive (
  input  D,
  input  en,
  output out_3,
  output out_4
);

  wire not_1_out;

  Flip_Flop__Negative flip_flop_negative_1 (.D(D), .en(not_1_out), .Q(out_3), .Q_prime(out_4));
  not not_1 (not_1_out, en);
endmodule

module Register (
  input  in,
  input  load,
  input  CLK,
  output Q,
  output Q_prime
);

  wire multiplexer_1_out;

  Multiplexer multiplexer_1 (.in0(Q), .in1(in), .out(multiplexer_1_out), .sel(load));  // open: en
  Flip_Flop__Positive flip_flop_positive_1 (.D(multiplexer_1_out), .en(CLK), .out_3(Q), .out_4(Q_prime));
endmodule

module one_shot (
  input  in,
  output out
);

  wire clock_1_out, register_1_q, register_2_q_prime;

  Register register_1 (.in(in), .load(1'b1), .CLK(clock_1_out), .Q(register_1_q));  // open: Q_prime
  Register register_2 (.in(register_1_q), .load(1'b1), .CLK(clock_1_out), .Q_prime(register_2_q_prime));  // open: Q
  Clock clock_1 (.out(clock_1_out));
  and and_1 (out, register_1_q, register_2_q_prime);
endmodule

module counter (
  input  reset,
  output [7:0] out_2
);

  wire clock_1_out;
  wire [7:0] adder_1_out, multiplexer_1_out;

  Multiplexer #(.width(8)) multiplexer_1 (
    .in0(adder_1_out), .in1({8{1'b0}}), .out(multiplexer_1_out), .sel(reset));  // open: en
  Register_part register_1 (.D(multiplexer_1_out), .Q(out_2), .clk(clock_1_out));  // open: en, clr
  Clock clock_1 (.out(clock_1_out));
  Adder adder_1 (.a(8'h1), .b(out_2), .out(adder_1_out));  // open: cin, cout
endmodule

module basic_RAM (
  input  [15:0] in,
  input  [1:0] address,
  input  load,
  output [15:0] out
);

  wire clock_1_out, demultiplexer_2_out0, demultiplexer_2_out1, demultiplexer_2_out2, demultiplexer_2_out3;
  wire [15:0] demultiplexer_1_out0, demultiplexer_1_out1, demultiplexer_1_out2, demultiplexer_1_out3,
       register_1_q, register_2_q, register_3_q, register_4_q;

  Demultiplexer #(.select(2), .width(16)) demultiplexer_1 (
    .out0(demultiplexer_1_out0), .out1(demultiplexer_1_out1), .out2(demultiplexer_1_out2),
    .out3(demultiplexer_1_out3), .in(in), .sel(address));  // open: en
  Demultiplexer #(.select(2)) demultiplexer_2 (
    .out0(demultiplexer_2_out0), .out1(demultiplexer_2_out1), .out2(demultiplexer_2_out2),
    .out3(demultiplexer_2_out3), .in(load), .sel(address));  // open: en
  Clock clock_1 (.out(clock_1_out));
  Register_part #(.width(16)) register_1 (
    .D(demultiplexer_1_out0), .en(demultiplexer_2_out0), .Q(register_1_q), .clk(clock_1_out));  // open: clr
  Register_part #(.width(16)) register_2 (
    .D(demultiplexer_1_out1), .en(demultiplexer_2_out1), .Q(register_2_q), .clk(clock_1_out));  // open: clr
  Register_part #(.width(16)) register_3 (
    .D(demultiplexer_1_out2), .en(demultiplexer_2_out2), .Q(register_3_q), .clk(clock_1_out));  // open: clr
  Register_part #(.width(16)) register_4 (
    .D(demultiplexer_1_out3), .en(demultiplexer_2_out3), .Q(register_4_q), .clk(clock_1_out));  // open: clr
  Multiplexer #(.select(2), .width(16)) multiplexer_1 (
    .in0(register_1_q), .in1(register_2_q), .in2(register_3_q), .in3(register_4_q), .out(out), .sel(address));  // open: en
endmodule

module XOR___NAND (
  input  a,
  input  b,
  output out_3,
  output out_4
);

  wire nand_1_out, nand_2_out, nand_3_out, nand_4_out, nand_5_out, nand_6_out, nand_7_out, nand_8_out,
       nand_9_out;

  nand nand_1 (nand_1_out, a, a);
  nand nand_2 (nand_2_out, nand_1_out, nand_3_out);
  nand nand_3 (nand_3_out, b, b);
  nand nand_4 (nand_4_out, b, a);
  nand nand_5 (nand_5_out, b, nand_6_out);
  nand nand_6 (nand_6_out, a, a);
  nand nand_7 (nand_7_out, b, b);
  nand nand_8 (nand_8_out, nand_7_out, a);
  nand nand_9 (nand_9_out, nand_2_out, nand_4_out);
  nand nand_10 (out_4, nand_5_out, nand_8_out);
  nand nand_11 (out_3, nand_9_out, nand_9_out);

  // Notes on the sheet:
  //   6 Gates starting with:
  //   (a v b)n(a' v b')
  //   5 Gates starting with:
  //   (a n b')v(a' n b)
endmodule
