// Logisim project P.circ as structural Verilog: 1 circuit, main circuit main
module main (
  input  [2:0] in_1
);

  wire and_1_out, and_2_out, and_3_out, and_4_out, and_5_out, and_6_out, and_7_out, and_8_out, and_9_out,
       nand_1_out, nand_2_out, nand_3_out, nand_4_out, nand_5_out, nand_6_out, nand_7_out, nand_8_out,
       nand_9_out, nand_10_out, nand_11_out, nand_12_out, nand_13_out, nand_14_out, nor_1_out, not_1_out,
       not_2_out, not_3_out, not_4_out, not_5_out, not_6_out, not_7_out, not_8_out, not_9_out, not_10_out,
       not_11_out, or_1_out, or_2_out, or_3_out, or_4_out, or_5_out, or_6_out, or_7_out, or_8_out;

  and and_1 (and_1_out, in_1[0], in_1[1]);
  not not_1 (not_1_out, in_1[2]);
  not not_2 (not_2_out, in_1[0]);
  not not_3 (not_3_out, in_1[1]);
  not not_4 (not_4_out, in_1[1]);
  not not_5 (not_5_out, in_1[1]);
  not not_6 (not_6_out, in_1[2]);
  not not_7 (not_7_out, in_1[1]);
  or or_1 (or_1_out, in_1[0], in_1[2]);
  not not_8 (not_8_out, in_1[0]);
  or or_2 (or_2_out, and_1_out, not_1_out);
  nand nand_1 (nand_1_out, in_1[0], in_1[1]);
  nand nand_2 (nand_2_out, nand_1_out, in_1[2]);
  nand nand_3 (nand_3_out, in_1[0], in_1[1]);
  nand nand_4 (nand_4_out, nand_3_out, in_1[2]);
  nand nand_5 (nand_5_out, in_1[0], in_1[1]);
  nand nand_6 (nand_6_out, nand_5_out, nand_7_out);
  nand nand_7 (nand_7_out, in_1[2], in_1[2]);
  nand nand_8 (nand_8_out, in_1[0], in_1[1]);
  nand nand_9 (nand_9_out, in_1[0], nand_10_out);
  nand nand_10 (nand_10_out, in_1[2], in_1[2]);
  and and_2 (and_2_out, not_2_out, not_3_out, in_1[2]);
  and and_3 (and_3_out, in_1[0], not_4_out, in_1[2]);
  and and_4 (and_4_out, in_1[0], not_5_out, not_6_out);
  and and_5 (and_5_out, not_7_out, or_1_out);
  or or_3 (or_3_out, in_1[0], in_1[2]);
  and and_6 (and_6_out, or_3_out, or_4_out);
  or or_4 (or_4_out, not_8_out, in_1[1]);
  // Probe on and_7_out
  and and_7 (and_7_out, or_2_out, in_1[0]);
  not not_9 (not_9_out, nand_11_out);
  nand nand_11 (nand_11_out, nand_2_out, in_1[0]);
  // Probe on not_9_out
  // Probe on nand_12_out
  nand nand_12 (nand_12_out, nand_4_out, in_1[0]);
  not not_10 (not_10_out, nand_13_out);
  nand nand_13 (nand_13_out, nand_6_out, in_1[0]);
  // Probe on not_10_out
  // Probe on nand_14_out
  nand nand_14 (nand_14_out, nand_8_out, nand_9_out);
  or or_5 (or_5_out, and_2_out, and_3_out, and_4_out);
  // Probe on or_5_out
  // Probe on and_5_out
  // Probe on and_6_out
  or or_6 (or_6_out, in_1[0], not_11_out);
  not not_11 (not_11_out, in_1[1]);
  and and_8 (and_8_out, in_1[1], in_1[2]);
  nor nor_1 (nor_1_out, in_1[0], in_1[1]);
  and and_9 (and_9_out, in_1[1], in_1[2]);
  or or_7 (or_7_out, or_6_out, and_8_out);
  // Probe on or_7_out
  // Probe on or_8_out
  or or_8 (or_8_out, nor_1_out, and_9_out);
endmodule
