// Logisim project RAM.circ as structural Verilog
module _8_word_RAM__16_bytes (
  input  [15:0] in,
  input  [2:0] address,
  input  CLK,
  input  load,
  output [15:0] out
);

  wire [7:0] demultiplexer_1_out7;
  wire [15:0] demultiplexer_2_out0, demultiplexer_2_out1, demultiplexer_2_out2, demultiplexer_2_out3,
       demultiplexer_2_out4, demultiplexer_2_out5, demultiplexer_2_out6, demultiplexer_2_out7,
       multiplexer_1_out, multiplexer_2_out, multiplexer_3_out, multiplexer_4_out, multiplexer_5_out,
       multiplexer_6_out, multiplexer_7_out, multiplexer_8_out, register_1_q, register_2_q, register_3_q,
       register_4_q, register_5_q, register_6_q, register_7_q, register_8_q;

  Demultiplexer #(.select(3)) demultiplexer_1 (
    .out0(demultiplexer_1_out7[7]), .out1(demultiplexer_1_out7[6]), .out2(demultiplexer_1_out7[5]),
    .out3(demultiplexer_1_out7[4]), .out4(demultiplexer_1_out7[3]), .out5(demultiplexer_1_out7[2]),
    .out6(demultiplexer_1_out7[1]), .out7(demultiplexer_1_out7[0]), .in(load), .sel(address));  // open: en
  Demultiplexer #(.select(3), .width(16)) demultiplexer_2 (
    .out0(demultiplexer_2_out0), .out1(demultiplexer_2_out1), .out2(demultiplexer_2_out2),
    .out3(demultiplexer_2_out3), .out4(demultiplexer_2_out4), .out5(demultiplexer_2_out5),
    .out6(demultiplexer_2_out6), .out7(demultiplexer_2_out7), .in(in), .sel(address));  // open: en
  Multiplexer #(.width(16)) multiplexer_1 (
    .in0(register_1_q), .in1(demultiplexer_2_out0), .out(multiplexer_1_out), .sel(demultiplexer_1_out7[7]));  // open: en
  Register #(.width(16)) register_1 (.D(multiplexer_1_out), .Q(register_1_q), .clk(CLK));  // open: en, clr
  Register #(.width(16)) register_2 (.D(multiplexer_2_out), .Q(register_2_q), .clk(CLK));  // open: en, clr
  Multiplexer #(.width(16)) multiplexer_2 (
    .in0(register_2_q), .in1(demultiplexer_2_out1), .out(multiplexer_2_out), .sel(demultiplexer_1_out7[6]));  // open: en
  Multiplexer #(.width(16)) multiplexer_3 (
    .in0(register_3_q), .in1(demultiplexer_2_out2), .out(multiplexer_3_out), .sel(demultiplexer_1_out7[5]));  // open: en
  Register #(.width(16)) register_3 (.D(multiplexer_3_out), .Q(register_3_q), .clk(CLK));  // open: en, clr
  Register #(.width(16)) register_4 (.D(multiplexer_4_out), .Q(register_4_q), .clk(CLK));  // open: en, clr
  Multiplexer #(.width(16)) multiplexer_4 (
    .in0(register_4_q), .in1(demultiplexer_2_out3), .out(multiplexer_4_out), .sel(demultiplexer_1_out7[4]));  // open: en
  Multiplexer #(.width(16)) multiplexer_5 (
    .in0(register_5_q), .in1(demultiplexer_2_out4), .out(multiplexer_5_out), .sel(demultiplexer_1_out7[3]));  // open: en
  Register #(.width(16)) register_5 (.D(multiplexer_5_out), .Q(register_5_q), .clk(CLK));  // open: en, clr
  Register #(.width(16)) register_6 (.D(multiplexer_6_out), .Q(register_6_q), .clk(CLK));  // open: en, clr
  Multiplexer #(.width(16)) multiplexer_6 (
    .in0(register_6_q), .in1(demultiplexer_2_out5), .out(multiplexer_6_out), .sel(demultiplexer_1_out7[2]));  // open: en
  Multiplexer #(.width(16)) multiplexer_7 (
    .in0(register_7_q), .in1(demultiplexer_2_out6), .out(multiplexer_7_out), .sel(demultiplexer_1_out7[1]));  // open: en
  Register #(.width(16)) register_7 (.D(multiplexer_7_out), .Q(register_7_q), .clk(CLK));  // open: en, clr
  Register #(.width(16)) register_8 (.D(multiplexer_8_out), .Q(register_8_q), .clk(CLK));  // open: en, clr
  Multiplexer #(.width(16)) multiplexer_8 (
    .in0(register_8_q), .in1(demultiplexer_2_out7), .out(multiplexer_8_out), .sel(demultiplexer_1_out7[0]));  // open: en
  Multiplexer #(.select(3), .width(16)) multiplexer_9 (
    .in0(register_1_q), .in1(register_2_q), .in2(register_3_q), .in3(register_4_q), .in4(register_5_q),
    .in5(register_6_q), .in6(register_7_q), .in7(register_8_q), .out(out), .sel(address));  // open: en
endmodule

module _64_word_RAM__128_bytes (
  input  load,
  input  [5:0] address,
  input  [15:0] in,
  input  CLK,
  output [15:0] out
);

  wire [2:0] demultiplexer_2_out0, demultiplexer_2_out1, demultiplexer_2_out2, demultiplexer_2_out3,
       demultiplexer_2_out4, demultiplexer_2_out5, demultiplexer_2_out6, demultiplexer_2_out7;
  wire [7:0] demultiplexer_1_out0;
  wire [15:0] demultiplexer_3_out0, demultiplexer_3_out1, demultiplexer_3_out2, demultiplexer_3_out3,
       demultiplexer_3_out4, demultiplexer_3_out5, demultiplexer_3_out6, demultiplexer_3_out7,
       n8_word_ram_16_bytes_1_out, n8_word_ram_16_bytes_2_out, n8_word_ram_16_bytes_3_out,
       n8_word_ram_16_bytes_4_out, n8_word_ram_16_bytes_5_out, n8_word_ram_16_bytes_6_out,
       n8_word_ram_16_bytes_7_out, n8_word_ram_16_bytes_8_out;

  Demultiplexer #(.select(3)) demultiplexer_1 (
    .out0(demultiplexer_1_out0[0]), .out1(demultiplexer_1_out0[1]), .out2(demultiplexer_1_out0[2]),
    .out3(demultiplexer_1_out0[3]), .out4(demultiplexer_1_out0[4]), .out5(demultiplexer_1_out0[5]),
    .out6(demultiplexer_1_out0[6]), .out7(demultiplexer_1_out0[7]), .in(load), .sel(address[2:0]));  // open: en
  Demultiplexer #(.select(3), .width(3)) demultiplexer_2 (
    .out0(demultiplexer_2_out0), .out1(demultiplexer_2_out1), .out2(demultiplexer_2_out2),
    .out3(demultiplexer_2_out3), .out4(demultiplexer_2_out4), .out5(demultiplexer_2_out5),
    .out6(demultiplexer_2_out6), .out7(demultiplexer_2_out7), .in(address[5:3]), .sel(address[2:0]));  // open: en
  Demultiplexer #(.select(3), .width(16)) demultiplexer_3 (
    .out0(demultiplexer_3_out0), .out1(demultiplexer_3_out1), .out2(demultiplexer_3_out2),
    .out3(demultiplexer_3_out3), .out4(demultiplexer_3_out4), .out5(demultiplexer_3_out5),
    .out6(demultiplexer_3_out6), .out7(demultiplexer_3_out7), .in(in), .sel(address[2:0]));  // open: en
  _8_word_RAM__16_bytes u_8_word_ram_16_bytes_1 (
    .in(demultiplexer_3_out0), .address(demultiplexer_2_out0), .load(demultiplexer_1_out0[0]), .CLK(CLK),
    .out(n8_word_ram_16_bytes_1_out));
  _8_word_RAM__16_bytes u_8_word_ram_16_bytes_2 (
    .in(demultiplexer_3_out1), .address(demultiplexer_2_out1), .load(demultiplexer_1_out0[1]), .CLK(CLK),
    .out(n8_word_ram_16_bytes_2_out));
  _8_word_RAM__16_bytes u_8_word_ram_16_bytes_3 (
    .in(demultiplexer_3_out2), .address(demultiplexer_2_out2), .load(demultiplexer_1_out0[2]), .CLK(CLK),
    .out(n8_word_ram_16_bytes_3_out));
  _8_word_RAM__16_bytes u_8_word_ram_16_bytes_4 (
    .in(demultiplexer_3_out3), .address(demultiplexer_2_out3), .load(demultiplexer_1_out0[3]), .CLK(CLK),
    .out(n8_word_ram_16_bytes_4_out));
  _8_word_RAM__16_bytes u_8_word_ram_16_bytes_5 (
    .in(demultiplexer_3_out4), .address(demultiplexer_2_out4), .load(demultiplexer_1_out0[4]), .CLK(CLK),
    .out(n8_word_ram_16_bytes_5_out));
  _8_word_RAM__16_bytes u_8_word_ram_16_bytes_6 (
    .in(demultiplexer_3_out5), .address(demultiplexer_2_out5), .load(demultiplexer_1_out0[5]), .CLK(CLK),
    .out(n8_word_ram_16_bytes_6_out));
  _8_word_RAM__16_bytes u_8_word_ram_16_bytes_7 (
    .in(demultiplexer_3_out6), .address(demultiplexer_2_out6), .load(demultiplexer_1_out0[6]), .CLK(CLK),
    .out(n8_word_ram_16_bytes_7_out));
  _8_word_RAM__16_bytes u_8_word_ram_16_bytes_8 (
    .in(demultiplexer_3_out7), .address(demultiplexer_2_out7), .load(demultiplexer_1_out0[7]), .CLK(CLK),
    .out(n8_word_ram_16_bytes_8_out));
  Multiplexer #(.select(3), .width(16)) multiplexer_1 (
    .in0(n8_word_ram_16_bytes_1_out), .in1(n8_word_ram_16_bytes_2_out), .in2(n8_word_ram_16_bytes_3_out),
    .in3(n8_word_ram_16_bytes_4_out), .in4(n8_word_ram_16_bytes_5_out), .in5(n8_word_ram_16_bytes_6_out),
    .in6(n8_word_ram_16_bytes_7_out), .in7(n8_word_ram_16_bytes_8_out), .out(out), .sel(address[2:0]));  // open: en

  // Notes on the sheet:
  //   First 3 bits select the correct RAM unit
  //   Second 3 select the address within that RAM unit
endmodule

// 1Kb
module _512_word_RAM__1Kb (
  input  load,
  input  [8:0] address,
  input  [15:0] in,
  input  CLK,
  output [15:0] out
);

  wire [5:0] demultiplexer_2_out0, demultiplexer_2_out1, demultiplexer_2_out2, demultiplexer_2_out3,
       demultiplexer_2_out4, demultiplexer_2_out5, demultiplexer_2_out6, demultiplexer_2_out7;
  wire [7:0] demultiplexer_1_out0;
  wire [15:0] _0_out, _2_out, _3_out, _4_out, _5_out, _6_out, _7_out, n64_word_ram_128_bytes_1_out;

  Demultiplexer #(.select(3)) demultiplexer_1 (
    .out0(demultiplexer_1_out0[0]), .out1(demultiplexer_1_out0[1]), .out2(demultiplexer_1_out0[2]),
    .out3(demultiplexer_1_out0[3]), .out4(demultiplexer_1_out0[4]), .out5(demultiplexer_1_out0[5]),
    .out6(demultiplexer_1_out0[6]), .out7(demultiplexer_1_out0[7]), .in(load), .sel(address[2:0]));  // open: en
  Demultiplexer #(.select(3), .width(6)) demultiplexer_2 (
    .out0(demultiplexer_2_out0), .out1(demultiplexer_2_out1), .out2(demultiplexer_2_out2),
    .out3(demultiplexer_2_out3), .out4(demultiplexer_2_out4), .out5(demultiplexer_2_out5),
    .out6(demultiplexer_2_out6), .out7(demultiplexer_2_out7), .in(address[8:3]), .sel(address[2:0]));  // open: en
  _64_word_RAM__128_bytes _0 (
    .load(demultiplexer_1_out0[0]), .address(demultiplexer_2_out0), .in(in), .CLK(CLK), .out(_0_out));
  _64_word_RAM__128_bytes u_64_word_ram_128_bytes_1 (
    .load(demultiplexer_1_out0[1]), .address(demultiplexer_2_out1), .in(in), .CLK(CLK),
    .out(n64_word_ram_128_bytes_1_out));
  _64_word_RAM__128_bytes _2 (
    .load(demultiplexer_1_out0[2]), .address(demultiplexer_2_out2), .in(in), .CLK(CLK), .out(_2_out));
  _64_word_RAM__128_bytes _3 (
    .load(demultiplexer_1_out0[3]), .address(demultiplexer_2_out3), .in(in), .CLK(CLK), .out(_3_out));
  Multiplexer #(.select(3), .width(16)) multiplexer_1 (
    .in0(_0_out), .in1(n64_word_ram_128_bytes_1_out), .in2(_2_out), .in3(_3_out), .in4(_4_out), .in5(_5_out),
    .in6(_6_out), .in7(_7_out), .out(out), .sel(address[2:0]));  // open: en
  _64_word_RAM__128_bytes _4 (
    .load(demultiplexer_1_out0[4]), .address(demultiplexer_2_out4), .in(in), .CLK(CLK), .out(_4_out));
  _64_word_RAM__128_bytes _5 (
    .load(demultiplexer_1_out0[5]), .address(demultiplexer_2_out5), .in(in), .CLK(CLK), .out(_5_out));
  _64_word_RAM__128_bytes _6 (
    .load(demultiplexer_1_out0[6]), .address(demultiplexer_2_out6), .in(in), .CLK(CLK), .out(_6_out));
  _64_word_RAM__128_bytes _7 (
    .load(demultiplexer_1_out0[7]), .address(demultiplexer_2_out7), .in(in), .CLK(CLK), .out(_7_out));
endmodule

// 8Kb
module _4096_word_RAM__8Kb (
  input  load,
  input  [11:0] address,
  input  [15:0] in,
  input  CLK,
  output [15:0] out
);

  wire [7:0] demultiplexer_1_out0;
  wire [8:0] demultiplexer_2_out0, demultiplexer_2_out1, demultiplexer_2_out2, demultiplexer_2_out3,
       demultiplexer_2_out4, demultiplexer_2_out5, demultiplexer_2_out6, demultiplexer_2_out7;
  wire [15:0] _0_out, _2_out, _3_out, _4_out, _5_out, _6_out, _7_out, n512_word_ram_1kb_1_out;

  Demultiplexer #(.select(3)) demultiplexer_1 (
    .out0(demultiplexer_1_out0[0]), .out1(demultiplexer_1_out0[1]), .out2(demultiplexer_1_out0[2]),
    .out3(demultiplexer_1_out0[3]), .out4(demultiplexer_1_out0[4]), .out5(demultiplexer_1_out0[5]),
    .out6(demultiplexer_1_out0[6]), .out7(demultiplexer_1_out0[7]), .in(load), .sel(address[2:0]));  // open: en
  Demultiplexer #(.select(3), .width(9)) demultiplexer_2 (
    .out0(demultiplexer_2_out0), .out1(demultiplexer_2_out1), .out2(demultiplexer_2_out2),
    .out3(demultiplexer_2_out3), .out4(demultiplexer_2_out4), .out5(demultiplexer_2_out5),
    .out6(demultiplexer_2_out6), .out7(demultiplexer_2_out7), .in(address[11:3]), .sel(address[2:0]));  // open: en
  _512_word_RAM__1Kb _0 (
    .load(demultiplexer_1_out0[0]), .address(demultiplexer_2_out0), .in(in), .CLK(CLK), .out(_0_out));
  _512_word_RAM__1Kb u_512_word_ram_1kb_1 (
    .load(demultiplexer_1_out0[1]), .address(demultiplexer_2_out1), .in(in), .CLK(CLK),
    .out(n512_word_ram_1kb_1_out));
  _512_word_RAM__1Kb _2 (
    .load(demultiplexer_1_out0[2]), .address(demultiplexer_2_out2), .in(in), .CLK(CLK), .out(_2_out));
  _512_word_RAM__1Kb _3 (
    .load(demultiplexer_1_out0[3]), .address(demultiplexer_2_out3), .in(in), .CLK(CLK), .out(_3_out));
  _512_word_RAM__1Kb _4 (
    .load(demultiplexer_1_out0[4]), .address(demultiplexer_2_out4), .in(in), .CLK(CLK), .out(_4_out));
  _512_word_RAM__1Kb _5 (
    .load(demultiplexer_1_out0[5]), .address(demultiplexer_2_out5), .in(in), .CLK(CLK), .out(_5_out));
  _512_word_RAM__1Kb _6 (
    .load(demultiplexer_1_out0[6]), .address(demultiplexer_2_out6), .in(in), .CLK(CLK), .out(_6_out));
  _512_word_RAM__1Kb _7 (
    .load(demultiplexer_1_out0[7]), .address(demultiplexer_2_out7), .in(in), .CLK(CLK), .out(_7_out));
  Multiplexer #(.select(3), .width(16)) multiplexer_1 (
    .in0(_0_out), .in1(n512_word_ram_1kb_1_out), .in2(_2_out), .in3(_3_out), .in4(_4_out), .in5(_5_out),
    .in6(_6_out), .in7(_7_out), .out(out), .sel(address[2:0]));  // open: en
endmodule

module _16384_word_RAM__32Kb (
  input  in_1,
  input  [13:0] address,
  input  [15:0] in,
  output [15:0] out_4
);

  wire CLK_out;
  wire [1:0] demultiplexer_1_out0, demultiplexer_1_out2;
  wire [11:0] demultiplexer_2_out0, demultiplexer_2_out1, demultiplexer_2_out2, demultiplexer_2_out3;
  wire [15:0] _0_out, _1_out, _2_out, _3_out;

  Clock CLK (.out(CLK_out));
  Demultiplexer #(.select(2)) demultiplexer_1 (
    .out0(demultiplexer_1_out0[0]), .out1(demultiplexer_1_out0[1]), .out2(demultiplexer_1_out2[0]),
    .out3(demultiplexer_1_out2[1]), .in(in_1), .sel(address[1:0]));  // open: en
  Demultiplexer #(.select(2), .width(12)) demultiplexer_2 (
    .out0(demultiplexer_2_out0), .out1(demultiplexer_2_out1), .out2(demultiplexer_2_out2),
    .out3(demultiplexer_2_out3), .in(address[13:2]), .sel(address[1:0]));  // open: en
  _4096_word_RAM__8Kb _0 (
    .load(demultiplexer_1_out0[0]), .address(demultiplexer_2_out0), .in(in), .CLK(CLK_out), .out(_0_out));
  _4096_word_RAM__8Kb _1 (
    .load(demultiplexer_1_out0[1]), .address(demultiplexer_2_out1), .in(in), .CLK(CLK_out), .out(_1_out));
  _4096_word_RAM__8Kb _2 (
    .load(demultiplexer_1_out2[0]), .address(demultiplexer_2_out2), .in(in), .CLK(CLK_out), .out(_2_out));
  _4096_word_RAM__8Kb _3 (
    .load(demultiplexer_1_out2[1]), .address(demultiplexer_2_out3), .in(in), .CLK(CLK_out), .out(_3_out));
  Multiplexer #(.select(2), .width(16)) multiplexer_1 (
    .in0(_0_out), .in1(_1_out), .in2(_2_out), .in3(_3_out), .out(out_4), .sel(address[1:0]));  // open: en
endmodule
